# Fritzing sketch Board (saved by Fritzing 0.9.1b)
breadboards: 1

parts:
  R1 = Resistor [tolerance=±5% resistance=4.7k package=THT]
  DS1 = DS18B20 1-Wire Temperature Sensor [part_number=DS18B20]
  J1 = T Cobbler Plus
  Rel1 = male pin header, 4 pins [form="♂ (male)"]
  Temp1 = male pin header, 3 pins [form="♂ (male)"]
  Temp2 = male pin header, 3 pins [form="♂ (male)"]
  Temp4 = male pin header, 3 pins [form="♂ (male)"]
  Water2 = male pin header, 4 pins [form="♂ (male)"]
  Water1 = male pin header, 4 pins [form="♂ (male)"]
  MCP3008 = IC, DIP package, 16 pins [chip_label=MCP3008]

nets:
  VDD: R1.Pin_0, DS1.VDD, J1.3V3, Temp1.pin3, Temp2.pin3, Temp4.pin3, Water2.pin1, Water1.pin1, MCP3008.pin15, MCP3008.pin16
  N1: R1.Pin_1, DS1.DQ, J1.#4, Temp1.pin2, Temp2.pin2, Temp4.pin2
  N2: DS1.GND, J1.GND#8, Temp1.pin1, Temp2.pin1, Temp4.pin1, Water2.pin2, Water1.pin2, MCP3008.pin14
  N3: J1.5.0V#1, Rel1.pin4
  N4: J1.GND#5, Rel1.pin3
  N5: J1.#17, Water2.pin3
  N6: J1.#18, Water1.pin3
  N7: J1.#23, Rel1.pin2
  N8: J1.3.3V, MCP3008.pin12
  N9: J1.#24, Rel1.pin1, MCP3008.pin9
  N10: J1.MOSI, MCP3008.pin11
  N11: J1.MISO, MCP3008.pin13
  N12: J1.#25, MCP3008.pin10
  N13: Water2.pin4, MCP3008.pin1
  N14: Water1.pin4, MCP3008.pin2

notes:
  GrowUp

custom parts:
  T Cobbler Plus: The T-Cobbler Plus is an add on prototyping board from Adafruit specifically designed for the Raspberry Pi B+ that can break out all those tasty power, GPIO, I2C and SPI pins from the 40-pin header onto a solderless breadboard. This set will make "cobbling together" prototypes with the Pi super easy. The T-Cobbler Plus can plug into any solderless breadboard.
